# Fritzing sketch devre şaması (saved by Fritzing 0.9.3b)
breadboards: 1

parts:
  S1 = H-Bridge with L298N
  DI1 = 7-Segment LED Display [package=THT]
  R1 = Photocell (LDR) [package=THT]
  R2 = Photocell (LDR) [package=THT]
  R10 = Resistor [tolerance=±5% resistance=220 package="2512 [SMD]"]
  R11 = Resistor [tolerance=±5% resistance=10k package="2512 [SMD]"]
  R12 = Resistor [tolerance=±5% resistance=10k package="2512 [SMD]"]
  R13 = Resistor [tolerance=±5% resistance=220 package="2512 [SMD]"]
  R14 = Resistor [tolerance=±5% resistance=220 package="2512 [SMD]"]
  R17 = Resistor [tolerance=±5% resistance=220 package="2512 [SMD]"]
  R18 = Resistor [tolerance=±5% resistance=220 package="2512 [SMD]"]
  R19 = Resistor [tolerance=±5% resistance=220 package="2512 [SMD]"]
  R20 = Resistor [tolerance=±5% resistance=220 package="2512 [SMD]"]
  M1 = DC Motor
  R21 = Photocell (LDR) [package=THT]
  R22 = Resistor [tolerance=±5% resistance=10k package="2512 [SMD]"]
  S5 = Pushbutton [package=THT]
  S6 = Pushbutton [package=THT]
  S7 = Pushbutton [package=THT]
  Parça3 = Arduino Uno (Rev3)
  R23 = Resistor [tolerance=±5% resistance=10k package="2512 [SMD]"]
  R24 = Resistor [tolerance=±5% resistance=10k package="2512 [SMD]"]
  R25 = Resistor [tolerance=±5% resistance=10k package="2512 [SMD]"]
  VCC1 = Battery

nets:
  N1: S1.GND, VCC1.-
  N2: S1.5V, VCC1.+
  N3: S1.IN1, Parça3.D11_PWM/MOSI
  N4: S1.IN2, Parça3.D10_PWM/SS
  N5: S1.M1-01, M1.pin_1
  N6: S1.M1-02, M1.pin_2
  N7: DI1.cathodeE, R13.Pin_0
  N8: DI1.cathodeD, R14.Pin_0
  N9: DI1.commAnode#2, R1.pin_1, R2.pin_1, R21.pin_1, Parça3.GND
  N10: DI1.cathodeC, R10.Pin_1
  N11: DI1.cathodeB, R19.Pin_1
  N12: DI1.cathodeA, R20.Pin_1
  N13: DI1.commAnode#7, R23.Pin_0, R24.Pin_0, R25.Pin_0
  N14: DI1.cathodeF, R18.Pin_0
  N15: DI1.cathodeG, R17.Pin_0
  N16: R1.pin_0, R11.Pin_0, Parça3.A1
  N17: R2.pin_0, R12.Pin_1, Parça3.A0
  N18: R10.Pin_0, Parça3.D7
  N19: R11.Pin_1, R12.Pin_0, R22.Pin_1
  N20: R13.Pin_1, Parça3.D5_PWM
  N21: R14.Pin_1, Parça3.D6_PWM
  N22: R17.Pin_1, Parça3.D13/SCK
  N23: R18.Pin_1, Parça3.D12/MISO
  N24: R19.Pin_0, Parça3.D8
  N25: R20.Pin_0, Parça3.D9_PWM
  N26: R21.pin_0, R22.Pin_0, Parça3.A2
  N27: S5.leg0, S6.leg0, S7.leg0, Parça3.5V, R23.Pin_1, R24.Pin_1, R25.Pin_1
  N28: S5.leg1, Parça3.D2
  N29: S6.leg1, Parça3.D3_PWM
  N30: S7.leg1, Parça3.D4

custom parts:
  H-Bridge with L298N: h-bridge

// code stored in the sketch: devre _amas_.fzz.ino
int
buton0 = 0,
buton1 = 1,
buton2 = 2,

kat0 = A0,
kat1 = A1,
kat2 = A2,
in1 = 3,
in2= 4,

A = 5, 
B = 6,
C = 7,
D = 8,
E = 9,
F = 10,
G = 11,
DP = 12;

boolean firstRun = true;
int currentFloor = 0; 
long debounceTime = 200; 
int kat1deger = 0; 
int kat2deger = 0;
 
byte numbers[3][8] = {{1,1,1,1,1,1,1,0},{0,1,1,0,0,0,0,0},{1,1,0,1,1,0,0,1}}; 
 
const int segments[8] = { A, B, C, D, E, f, G, DP }; 

void setup(){
  Serial.begin(9600);

//--------------------I/O'LAR AYARLANIYOR------------------//
  pinMode(buton1, INPUT);
  pinMode(buton2, INPUT);
  pinMode(buton3, INPUT);
  
  pinMode(kat1, INPUT);
  pinMode(kat2, INPUT);
  
  pinMode(in1, OUTPUT);
  pinMode(in2, OUTPUT);
  
  pinMode(A, OUTPUT);
  pinMode(B, OUTPUT);
  pinMode(C, OUTPUT);
  pinMode(D, OUTPUT);
  pinMode(E, OUTPUT);
  pinMode(F, OUTPUT);
  pinMode(G, OUTPUT);
  pinMode(DP, OUTPUT);

//---------------------BASLANGIC SET AYARLARI YAPILIYOR-----------------------//
  digitalWrite(A, LOW);
  digitalWrite(B, LOW);
  digitalWrite(C, LOW);
  digitalWrite(D, LOW);
  digitalWrite(E, LOW);
  digitalWrite(F, LOW);
  digitalWrite(G, LOW);
  digitalWrite(DP, LOW);
  
}


//-------------------MOTOR DURUMLARI AYARLANIYOR-------------------------------//
void ileri(){
  digitalWrite(in1, HIGH);
  digitalWrite(in2, LOW);
}

void geri(){
  digitalWrite(in1, LOW);
  digitalWrite(in2, HIGH);
}

void dur(){
  digitalWrite(in1, LOW);
  digitalWrite(in2, LOW);
}

void loop(){
  kat0deger = analogRead (kat0);
  kat1deger = analogRead (kat1);
  kat2deger = analogRead (kat2);

  Serial.print("Analog Deger (Birinci kat) = ");
  Serial.println(kat1deger);
  Serial.print("Analog Deger (Ikinci kat) = ");
  Serial.println(kat2deger);
  delay(1000);

//------------------------DISPLAY KONTROL EDILIYOR--------------------------//

  if(kat0deger < 750) {
    setSegments(0, CC4); 
    currentFloor = 0;                    
  } 
  
  else if(kat1deger < 750) {
    setSegments(1, CC4); 
    currentFloor = 1;
  }
  
  else if(kat2deger < 750){
    setSegments(2, CC4);
    currentFloor = 2;
  }
  
    currentFloor = 0; // Sets the currentFloor to 1 since the elevator is now at the first floor
    delay(1000);
  }

//-----------------------------ASANSOR KONTROL EDILIYOR--------------------------//

//----------------------------ZEMIN KATA BASILDIGINDA------------------------------------------//
    if(readSwitch(buton0, debounceTime) == true && currentFloor != 2){
     
    if(currentFloor == 1){
      Serial.println("iniyor");
      geri();
       
      while(kat0deger < 750){
        dur();
      }
    }
    else if(currentFloor == 2){
      Serial.println("iniyor");
      geri();
       
      while(kat0deger > 750){
        dur();
      }
    }
    currentFloor = 0; // Sets the currentFloor to 2 since the elevator is now at the second floor
    delay(2000);
  }

  
//-------------------------------BIRINCI KATA BASILDIGINDA----------------------------------------//
  if(readSwitch(buton1, debounceTime) == true && currentFloor != 1){
     
    if(currentFloor == 0){
      Serial.println("cikiyor");
      ileri();
       
      while(kat1deger < 750){
        dur();
      }
    }
    else if(currentFloor == 2){
      Serial.println("iniyor");
      geri();
       
      while(kat1deger > 750){
        dur();
      }
    }
    currentFloor = 1; // Sets the currentFloor to 2 since the elevator is now at the second floor
    delay(2000);
  }

  
//-----------------------------------IKINCI KATA BASILDIGINDA-----------------------------------------//
    if(readSwitch(buton2, debounceTime) == true && currentFloor != 2){
     
    if(currentFloor == 0){
      Serial.println("cikiyor");
      ileri();
       
      while(kat2deger < 750){
        dur();
      }
    }
    else if(currentFloor == 1){
      Serial.println("cikiyor");
      ileri();
       
      while(kat2deger > 750){
        dur();
      }
    }
    currentFloor = 2; // Sets the currentFloor to 2 since the elevator is now at the second floor
    delay(2000);
  }
