# Fritzing sketch BağlantıŞeması (saved by Fritzing 0.9.3b)
breadboards: 1

parts:
  Parça1 = Arduino Uno (Rev3) - ICSP
  M1 = DC Motor
  M2 = DC Motor
  S1 = H-Bridge with L298N

nets:
  N1: Parça1.D8, S1.IN3
  N2: Parça1.D9_PWM, S1.IN4
  N3: Parça1.D6_PWM, S1.IN1
  N4: Parça1.D7, S1.IN2
  5V: Parça1.5V, S1.5V
  GND: Parça1.GND, S1.GND
  N5: M1.pin_1, S1.ENB-5V
  N6: M1.pin_2, S1.ENB
  N7: M2.pin_1, S1.ENA-5V
  N8: M2.pin_2, S1.ENA

custom parts:
  H-Bridge with L298N: h-bridge
