# Fritzing sketch devre (saved by Fritzing 0.9.2b)
breadboards: 1

parts:
  Eleman1 = Arduino Uno (Rev3)
  LCD1 = LCD screen
  R1 = Rotary Potentiometer (Small) [maximum_resistance=100kΩ package=THT]
  R2 = Rotary Potentiometer (Small) [maximum_resistance=100kΩ package=THT]
  S1 = Momentary Switch [package=ksa_sealed_tac_switch]
  R3 = Resistor [tolerance=±5% resistance=220 package=THT]
  J1 = Piezo Speaker

nets:
  N1: Eleman1.A0, R1.wiper
  N2: Eleman1.D8, S1.4
  N3: Eleman1.D10_PWM/SS, J1.pin2
  N4: Eleman1.D11_PWM/MOSI, LCD1.E
  N5: Eleman1.D12/MISO, LCD1.RS
  N6: Eleman1.D2, LCD1.DB7
  N7: Eleman1.D3_PWM, LCD1.DB6
  N8: Eleman1.D4, LCD1.DB5
  N9: Eleman1.D5_PWM, LCD1.DB4
  5V: Eleman1.5V, LCD1.VDD, LCD1.LED+, R1.leg1, R2.leg2, S1.1
  GND: Eleman1.GND, LCD1.VSS, LCD1.R/W, LCD1.LED-, R1.leg2, R2.leg1, R3.Pin_0, J1.pin1
  N10: LCD1.V0, R2.wiper
  N11: S1.3, R3.Pin_1
